# Fritzing sketch IoT Tracker (saved by Fritzing 0.9.2b)
breadboards: 1

parts:
  Part1 = Logic Level Converter
  Part2 = Arduino Uno (Rev3)
  J1 = Basic Servo
  J2 = Basic Servo
  R1 = Photocell (LDR) [package=THT]
  R2 = Photocell (LDR) [package=THT]
  R3 = Photocell (LDR) [package=THT]
  R4 = Photocell (LDR) [package=THT]
  R5 = Resistor [tolerance=±5% resistance=5.6k package="2010 [SMD]"]
  R6 = Resistor [tolerance=±5% resistance=5.6k package="2010 [SMD]"]
  R7 = Resistor [tolerance=±5% resistance=5.6k package="2010 [SMD]"]
  R8 = Resistor [tolerance=±5% resistance=5.6k package="2010 [SMD]"]
  IC1 = IC, DIP package, 16 pins [chip_label=IC part_number=MCP3008]
  R9 = Resistor [tolerance=±1% resistance=200 package=THT]
  J3 = Screw terminal - 2 pins [package=THT]
  J4 = Screw terminal - 2 pins [package=THT]
  R10 = Resistor [tolerance=±1% resistance=110 package=THT]
  R11 = Resistor [tolerance=±1% resistance=110 package=THT]
  R12 = Resistor [tolerance=±1% resistance=1k package=THT]
  J5 = screw terminal, 3 pins
  Raspberry_Pi1 = Raspberry Pi 2

nets:
  GND: Part1.GND, Part2.GND, J1.gnd, J2.gnd, R1.pin_1, R2.pin_1, R3.pin_1, R4.pin_1, IC1.pin9, IC1.pin14, J4.pin2, R10.Pin_1, R12.Pin_1, J5.pin3, Raspberry_Pi1.GND
  N1: Part1.LV, IC1.pin15, IC1.pin16, J5.pin2, Raspberry_Pi1.3v3
  N2: Part1.RX_LV, Raspberry_Pi1.GPIO2
  N3: Part1.TX_LV, Raspberry_Pi1.GPIO3
  N4: Part1.TX_HV, Part2.A5/SCL
  N5: Part1.RX_HV, Part2.A4/SDA
  VCC: Part1.HV, Part2.5V, J1.vcc, J2.vcc, R5.Pin_0, R6.Pin_0, R7.Pin_0, R8.Pin_0
  N6: Part2.A0, R2.pin_0, R8.Pin_1
  N7: Part2.A1, R1.pin_0, R5.Pin_1
  N8: Part2.A2, R3.pin_0, R6.Pin_1
  N9: Part2.A3, R4.pin_0, R7.Pin_1
  N10: Part2.D10_PWM/SS, J2.pulse
  N11: Part2.D11_PWM/MOSI, J1.pulse
  N12: IC1.pin1, R9.Pin_1, R10.Pin_0
  N13: IC1.pin2, R11.Pin_1, R12.Pin_0
  N14: IC1.pin3, J5.pin1
  N15: IC1.pin10, Raspberry_Pi1.GPIO8
  N16: IC1.pin11, Raspberry_Pi1.GPIO10
  N17: IC1.pin12, Raspberry_Pi1.GPIO9
  N18: IC1.pin13, Raspberry_Pi1.GPIO11
  N19: R9.Pin_0, J3.pin1
  N20: J4.pin1, R11.Pin_0

notes:
  5 VOLT LINE
  3.3 VOLT LINE
